// Digital circuit 64-bit-reg-clr.dig as structural Verilog
module _64_bit_reg_clr (
  input  CLR,
  input  [63:0] D,
  input  CLK,
  input  EN,
  output [63:0] Q
);

  wire or_1_out, or_2_out;
  wire [63:0] multiplexer_1_out;

  Multiplexer #(.Bits(64)) multiplexer_1 (.sel(CLR), .in_0(D), .in_1({64{1'b0}}), .out(multiplexer_1_out));
  or or_1 (or_1_out, CLK, CLR);
  or or_2 (or_2_out, EN, CLR);
  Register #(.Bits(64)) register_1 (.D(multiplexer_1_out), .C(or_1_out), .en(or_2_out), .Q(Q));
endmodule
