// Digital circuit alu.dig as structural Verilog
module alu (
  input  [63:0] A,
  input  [63:0] B,
  input  [3:0] OP,
  output [63:0] R
);

  wire [63:0] add_1_s, and_1_out, bitextender_1_out, mul64_1_p, multiplexer_1_out, or_1_out, SLL_out,
       SRL_out, sub_1_s;

  Multiplexer #(.Selector_Bits(3), .Bits(64)) multiplexer_1 (
    .sel(OP[2:0]), .in_0(add_1_s), .in_1(sub_1_s), .in_2(mul64_1_p), .in_3(SLL_out), .in_4(SRL_out),
    .in_5(or_1_out), .in_6(and_1_out), .in_7(B), .out(multiplexer_1_out));
  Add #(.Bits(64)) add_1 (.a(A), .b(B), .c_i(1'b0), .s(add_1_s));  // open: c_o
  Sub #(.Bits(64)) sub_1 (.a(A), .b(B), .c_i(1'b0), .s(sub_1_s));  // open: c_o
  BitExtender #(.inputBits(32), .outputBits(64)) bitextender_1 (.in(multiplexer_1_out[31:0]), .out(bitextender_1_out));
  mul64 mul64_1 (.A(A), .B(B), .P(mul64_1_p));
  BarrelShifter #(.Bits(64)) SLL (.in(A), .shift({1'b0, B[5:0]}), .out(SLL_out));
  Multiplexer #(.Bits(64)) multiplexer_2 (.sel(OP[3]), .in_0(multiplexer_1_out), .in_1(bitextender_1_out), .out(R));
  BarrelShifter #(.Bits(64), .direction("right")) SRL (.in(A), .shift({1'b0, B[5:0]}), .out(SRL_out));
  assign or_1_out = A | B;  // Or or_1, 64 bits wide
  assign and_1_out = A & B;  // And and_1, 64 bits wide
endmodule
