// Digital circuit imm-decoder.dig as structural Verilog
module imm_decoder (
  input  [31:0] IW,
  output [63:0] imm_i,
  output [63:0] imm_s,
  output [63:0] imm_b,
  output [63:0] imm_u,
  output [63:0] imm_j,
  output [63:0] shamt
);

  BitExtender #(.inputBits(12), .outputBits(64)) bitextender_1 (.in(IW[31:20]), .out(imm_i));
  BitExtender #(.inputBits(12), .outputBits(64)) bitextender_2 (.in({IW[31:25], IW[11:7]}), .out(imm_s));
  BitExtender #(.inputBits(13), .outputBits(64)) bitextender_3 (
    .in({IW[31], IW[7], IW[30:25], IW[11:8], 1'b0}), .out(imm_b));
  BitExtender #(.inputBits(32), .outputBits(64)) bitextender_4 (.in({IW[31:12], {12{1'b0}}}), .out(imm_u));
  BitExtender #(.inputBits(21), .outputBits(64)) bitextender_5 (
    .in({IW[31], IW[19:12], IW[20], IW[30:21], 1'b0}), .out(imm_j));

  assign shamt = {{58{1'b0}}, IW[25:20]};
endmodule
