// Digital circuit inst-decoder.dig as structural Verilog
module inst_decoder (
  input  [31:0] IW,
  output [1:0] PCsel,
  output [2:0] ALUSrcB,
  output ALUSrcA,
  output [3:0] ALUOp,
  output RFW,
  output WDsel,
  output [2:0] BrOp,
  output [1:0] SZ,
  output ST,
  output LD,
  output m2r
);

  wire ADDI_eq, ADDIW_eq, ADDR_eq, ANDR_eq, BEQ_eq, BGE_eq, BLT_eq, BNE_eq, jal_eq_1_eq, jalr_eq_1_eq, LB_eq,
       LD_eq, LUI_eq, LW_eq, MUL_eq, ORR_eq, SB_eq, SD_eq, SLLI_eq, SLLR_eq, SRLI_eq, SRLR_eq, SUB_eq, SW_eq;
  wire [4:0] priorityencoder_1_num;

  opcode_funct3_funct7_eq ADDR (
    .iw_opcode(IW[6:0]), .iw_funct3(IW[14:12]), .iw_funct7(IW[31:25]), .funct7({7{1'b0}}),
    .opcode(7'b0110011), .funct3(3'b000), .eq(ADDR_eq));
  opcode_funct3_funct7_eq SUB (
    .iw_opcode(IW[6:0]), .iw_funct3(IW[14:12]), .iw_funct7(IW[31:25]), .funct7(7'b0100000),
    .opcode(7'b0110011), .funct3(3'b000), .eq(SUB_eq));
  opcode_funct3_funct7_eq MUL (
    .iw_opcode(IW[6:0]), .iw_funct3(IW[14:12]), .iw_funct7(IW[31:25]), .funct7(7'b0000001),
    .opcode(7'b0110011), .funct3(3'b000), .eq(MUL_eq));
  opcode_funct3_eq SLLR (
    .iw_opcode(IW[6:0]), .iw_funct3(IW[14:12]), .funct3(3'b001), .opcode(7'b0110011), .eq(SLLR_eq));
  opcode_funct3_eq SRLR (
    .iw_opcode(IW[6:0]), .iw_funct3(IW[14:12]), .funct3(3'b101), .opcode(7'b0110011), .eq(SRLR_eq));
  opcode_funct3_funct7_eq ORR (
    .iw_opcode(IW[6:0]), .iw_funct3(IW[14:12]), .iw_funct7(IW[31:25]), .funct7({7{1'b0}}),
    .opcode(7'b0110011), .funct3(3'b110), .eq(ORR_eq));
  opcode_funct3_funct7_eq ANDR (
    .iw_opcode(IW[6:0]), .iw_funct3(IW[14:12]), .iw_funct7(IW[31:25]), .funct7({7{1'b0}}),
    .opcode(7'b0110011), .funct3(3'b111), .eq(ANDR_eq));
  opcode_funct3_eq ADDI (
    .iw_opcode(IW[6:0]), .iw_funct3(IW[14:12]), .funct3(3'b000), .opcode(7'b0010011), .eq(ADDI_eq));
  opcode_funct3_funct6_eq SLLI (
    .iw_opcode(IW[6:0]), .iw_funct3(IW[14:12]), .iw_funct6(IW[31:26]), .funct6({6{1'b0}}),
    .opcode(7'b0010011), .funct3(3'b001), .eq(SLLI_eq));
  opcode_funct3_funct6_eq SRLI (
    .iw_opcode(IW[6:0]), .iw_funct3(IW[14:12]), .iw_funct6(IW[31:26]), .funct6({6{1'b0}}),
    .opcode(7'b0010011), .funct3(3'b101), .eq(SRLI_eq));
  opcode_funct3_eq ADDIW (
    .iw_opcode(IW[6:0]), .iw_funct3(IW[14:12]), .funct3(3'b000), .opcode(7'b0011011), .eq(ADDIW_eq));
  opcode_funct3_eq LB (.iw_opcode(IW[6:0]), .iw_funct3(IW[14:12]), .funct3(3'b000), .opcode(7'b0000011), .eq(LB_eq));
  opcode_funct3_eq LW (.iw_opcode(IW[6:0]), .iw_funct3(IW[14:12]), .funct3(3'b010), .opcode(7'b0000011), .eq(LW_eq));
  opcode_funct3_eq u_LD (.iw_opcode(IW[6:0]), .iw_funct3(IW[14:12]), .funct3(3'b011), .opcode(7'b0000011), .eq(LD_eq));
  opcode_funct3_eq SB (.iw_opcode(IW[6:0]), .iw_funct3(IW[14:12]), .funct3(3'b000), .opcode(7'b0100011), .eq(SB_eq));
  opcode_funct3_eq SW (.iw_opcode(IW[6:0]), .iw_funct3(IW[14:12]), .funct3(3'b010), .opcode(7'b0100011), .eq(SW_eq));
  opcode_funct3_eq SD (.iw_opcode(IW[6:0]), .iw_funct3(IW[14:12]), .funct3(3'b011), .opcode(7'b0100011), .eq(SD_eq));
  opcode_funct3_eq BEQ (.iw_opcode(IW[6:0]), .iw_funct3(IW[14:12]), .funct3(3'b000), .opcode(7'b1100011), .eq(BEQ_eq));
  opcode_funct3_eq BNE (.iw_opcode(IW[6:0]), .iw_funct3(IW[14:12]), .funct3(3'b001), .opcode(7'b1100011), .eq(BNE_eq));
  opcode_funct3_eq BLT (.iw_opcode(IW[6:0]), .iw_funct3(IW[14:12]), .funct3(3'b100), .opcode(7'b1100011), .eq(BLT_eq));
  opcode_funct3_eq BGE (.iw_opcode(IW[6:0]), .iw_funct3(IW[14:12]), .funct3(3'b101), .opcode(7'b1100011), .eq(BGE_eq));
  jal_eq jal_eq_1 (.opcode(IW[6:0]), .eq(jal_eq_1_eq));
  Comparator #(.Bits(7)) LUI (.a(IW[6:0]), .b(7'b0110111), .eq(LUI_eq));  // open: gt, lt
  jalr_eq jalr_eq_1 (.opcode(IW[6:0]), .funct3(IW[14:12]), .eq(jalr_eq_1_eq));
  PriorityEncoder #(.Selector_Bits(5)) priorityencoder_1 (
    .in0(ADDR_eq), .in1(SUB_eq), .in2(MUL_eq), .in3(SLLR_eq), .in4(SRLR_eq), .in5(ORR_eq), .in6(ANDR_eq),
    .in7(ADDI_eq), .in8(SLLI_eq), .in9(SRLI_eq), .in10(ADDIW_eq), .in11(LB_eq), .in12(LW_eq), .in13(LD_eq),
    .in14(SB_eq), .in15(SW_eq), .in16(SD_eq), .in17(BEQ_eq), .in18(BNE_eq), .in19(BLT_eq), .in20(BGE_eq),
    .in21(LUI_eq), .in22(jal_eq_1_eq), .in23(jalr_eq_1_eq), .in24(1'b0), .in25(1'b0), .in26(1'b0),
    .in27(1'b0), .in28(1'b0), .in29(1'b0), .in30(1'b0), .in31(1'b0), .num(priorityencoder_1_num));  // open: any
  ROM #(.AddrBits(5), .Bits(20)) rom_1 (
    .A(priorityencoder_1_num), .sel(1'b1),
    .D({WDsel, RFW, BrOp, ALUSrcB, ALUSrcA, ALUOp, m2r, LD, ST, SZ, PCsel}));

  // Notes on the sheet:
  //   contents of rom_1 (hex, n*v repeats v):
  //   c0000,c0080,c0100,c0180,c0200,c0280,c0300,c1000,c1180,c1200,c1400
  //   ,c1060,c1068,c106c,82030,82038,8203c,8b801,93801,9b801,a3801,c4380
  //   ,6d801,69001
endmodule
