// Digital circuit jal-eq.dig as structural Verilog
module jal_eq (
  input  [6:0] opcode,
  output eq
);

  Comparator #(.Bits(7)) comparator_1 (.a(opcode), .b(7'b1101111), .eq(eq));  // open: gt, lt
endmodule
