// Digital circuit mul64.dig as structural Verilog
module mul64 (
  input  [63:0] A,
  input  [63:0] B,
  output [63:0] P
);

  wire [31:0] add_1_s;
  wire [63:0] mul_1_mul, mul_2_mul, mul_3_mul;

  Mul #(.Bits(32)) mul_1 (.a(A[31:0]), .b(B[31:0]), .mul(mul_1_mul));
  Mul #(.Bits(32)) mul_2 (.a(A[31:0]), .b(B[63:32]), .mul(mul_2_mul));
  Mul #(.Bits(32)) mul_3 (.a(A[63:32]), .b(B[31:0]), .mul(mul_3_mul));
  Add #(.Bits(32)) add_1 (.a(mul_2_mul[31:0]), .b(mul_3_mul[31:0]), .c_i(1'b0), .s(add_1_s));  // open: c_o
  Add #(.Bits(64)) add_2 (.a(mul_1_mul), .b({add_1_s, {32{1'b0}}}), .c_i(1'b0), .s(P));  // open: c_o
endmodule
