// Digital circuit opcode-funct3-eq.dig as structural Verilog
module opcode_funct3_eq (
  input  [6:0] iw_opcode,
  input  [2:0] iw_funct3,
  input  [2:0] funct3,
  input  [6:0] opcode,
  output eq
);

  wire funct3_eq, opcode_eq;

  Comparator #(.Bits(3)) u_funct3 (.a(funct3), .b(iw_funct3), .eq(funct3_eq));  // open: gt, lt
  Comparator #(.Bits(7)) u_opcode (.a(opcode), .b(iw_opcode), .eq(opcode_eq));  // open: gt, lt
  and and_1 (eq, funct3_eq, opcode_eq);
endmodule
