// Digital circuit opcode-funct3-funct6-eq.dig as structural Verilog
module opcode_funct3_funct6_eq (
  input  [6:0] iw_opcode,
  input  [2:0] iw_funct3,
  input  [5:0] iw_funct6,
  input  [5:0] funct6,
  input  [6:0] opcode,
  input  [2:0] funct3,
  output eq
);

  wire funct3_eq, funct6_eq, opcode_eq;

  Comparator #(.Bits(7)) u_opcode (.a(iw_opcode), .b(opcode), .eq(opcode_eq));  // open: gt, lt
  Comparator #(.Bits(3)) u_funct3 (.a(iw_funct3), .b(funct3), .eq(funct3_eq));  // open: gt, lt
  Comparator #(.Bits(6)) u_funct6 (.a(iw_funct6), .b(funct6), .eq(funct6_eq));  // open: gt, lt
  and and_1 (eq, opcode_eq, funct3_eq, funct6_eq);
endmodule
