// Digital circuit reg-file.dig as structural Verilog
module reg_file (
  input  [4:0] RR1,
  input  [4:0] RR0,
  input  CLK,
  input  CLR,
  input  WEN,
  input  [63:0] WD,
  input  [4:0] WREG,
  output [63:0] RD0,
  output [63:0] RD1,
  output [63:0] X0,
  output [63:0] X1,
  output [63:0] X2,
  output [63:0] X3,
  output [63:0] X4,
  output [63:0] X5,
  output [63:0] X6,
  output [63:0] X7,
  output [63:0] X8,
  output [63:0] X9,
  output [63:0] X10,
  output [63:0] X11,
  output [63:0] X12,
  output [63:0] X13,
  output [63:0] X14,
  output [63:0] X15,
  output [63:0] X16,
  output [63:0] X17,
  output [63:0] X18,
  output [63:0] X19,
  output [63:0] X20,
  output [63:0] X21,
  output [63:0] X22,
  output [63:0] X23,
  output [63:0] X24,
  output [63:0] X25,
  output [63:0] X26,
  output [63:0] X27,
  output [63:0] X28,
  output [63:0] X29,
  output [63:0] X30,
  output [63:0] X31
);

  wire decoder_1_out_1, decoder_1_out_2, decoder_1_out_3, decoder_1_out_4, decoder_1_out_5, decoder_1_out_6,
       decoder_1_out_7, decoder_1_out_8, decoder_1_out_9, decoder_1_out_10, decoder_1_out_11,
       decoder_1_out_12, decoder_1_out_13, decoder_1_out_14, decoder_1_out_15, decoder_1_out_16,
       decoder_1_out_17, decoder_1_out_18, decoder_1_out_19, decoder_1_out_20, decoder_1_out_21,
       decoder_1_out_22, decoder_1_out_23, decoder_1_out_24, decoder_1_out_25, decoder_1_out_26,
       decoder_1_out_27, decoder_1_out_28, decoder_1_out_29, decoder_1_out_30, decoder_1_out_31;
  wire [4:0] multiplexer_1_out;

  Multiplexer #(.Bits(5)) multiplexer_1 (.sel(WEN), .in_0({5{1'b0}}), .in_1(WREG), .out(multiplexer_1_out));
  Decoder #(.Selector_Bits(5)) decoder_1 (
    .sel(multiplexer_1_out), .out_1(decoder_1_out_1), .out_2(decoder_1_out_2), .out_3(decoder_1_out_3),
    .out_4(decoder_1_out_4), .out_5(decoder_1_out_5), .out_6(decoder_1_out_6), .out_7(decoder_1_out_7),
    .out_8(decoder_1_out_8), .out_9(decoder_1_out_9), .out_10(decoder_1_out_10), .out_11(decoder_1_out_11),
    .out_12(decoder_1_out_12), .out_13(decoder_1_out_13), .out_14(decoder_1_out_14),
    .out_15(decoder_1_out_15), .out_16(decoder_1_out_16), .out_17(decoder_1_out_17),
    .out_18(decoder_1_out_18), .out_19(decoder_1_out_19), .out_20(decoder_1_out_20),
    .out_21(decoder_1_out_21), .out_22(decoder_1_out_22), .out_23(decoder_1_out_23),
    .out_24(decoder_1_out_24), .out_25(decoder_1_out_25), .out_26(decoder_1_out_26),
    .out_27(decoder_1_out_27), .out_28(decoder_1_out_28), .out_29(decoder_1_out_29),
    .out_30(decoder_1_out_30), .out_31(decoder_1_out_31));  // open: out_0
  _64_bit_reg_clr u_X1 (.CLR(CLR), .D(WD), .CLK(CLK), .EN(decoder_1_out_1), .Q(X1));
  _64_bit_reg_clr u_X2 (.CLR(CLR), .D(WD), .CLK(CLK), .EN(decoder_1_out_2), .Q(X2));
  _64_bit_reg_clr u_X3 (.CLR(CLR), .D(WD), .CLK(CLK), .EN(decoder_1_out_3), .Q(X3));
  _64_bit_reg_clr u_X4 (.CLR(CLR), .D(WD), .CLK(CLK), .EN(decoder_1_out_4), .Q(X4));
  _64_bit_reg_clr u_X5 (.CLR(CLR), .D(WD), .CLK(CLK), .EN(decoder_1_out_5), .Q(X5));
  _64_bit_reg_clr u_X6 (.CLR(CLR), .D(WD), .CLK(CLK), .EN(decoder_1_out_6), .Q(X6));
  _64_bit_reg_clr u_X7 (.CLR(CLR), .D(WD), .CLK(CLK), .EN(decoder_1_out_7), .Q(X7));
  _64_bit_reg_clr u_X8 (.CLR(CLR), .D(WD), .CLK(CLK), .EN(decoder_1_out_8), .Q(X8));
  _64_bit_reg_clr u_X9 (.CLR(CLR), .D(WD), .CLK(CLK), .EN(decoder_1_out_9), .Q(X9));
  _64_bit_reg_clr u_X10 (.CLR(CLR), .D(WD), .CLK(CLK), .EN(decoder_1_out_10), .Q(X10));
  _64_bit_reg_clr u_X11 (.CLR(CLR), .D(WD), .CLK(CLK), .EN(decoder_1_out_11), .Q(X11));
  _64_bit_reg_clr u_X12 (.CLR(CLR), .D(WD), .CLK(CLK), .EN(decoder_1_out_12), .Q(X12));
  _64_bit_reg_clr u_X13 (.CLR(CLR), .D(WD), .CLK(CLK), .EN(decoder_1_out_13), .Q(X13));
  _64_bit_reg_clr u_X14 (.CLR(CLR), .D(WD), .CLK(CLK), .EN(decoder_1_out_14), .Q(X14));
  _64_bit_reg_clr u_X15 (.CLR(CLR), .D(WD), .CLK(CLK), .EN(decoder_1_out_15), .Q(X15));
  _64_bit_reg_clr u_X16 (.CLR(CLR), .D(WD), .CLK(CLK), .EN(decoder_1_out_16), .Q(X16));
  _64_bit_reg_clr u_X17 (.CLR(CLR), .D(WD), .CLK(CLK), .EN(decoder_1_out_17), .Q(X17));
  _64_bit_reg_clr u_X18 (.CLR(CLR), .D(WD), .CLK(CLK), .EN(decoder_1_out_18), .Q(X18));
  _64_bit_reg_clr u_X19 (.CLR(CLR), .D(WD), .CLK(CLK), .EN(decoder_1_out_19), .Q(X19));
  _64_bit_reg_clr u_X20 (.CLR(CLR), .D(WD), .CLK(CLK), .EN(decoder_1_out_20), .Q(X20));
  _64_bit_reg_clr u_X21 (.CLR(CLR), .D(WD), .CLK(CLK), .EN(decoder_1_out_21), .Q(X21));
  _64_bit_reg_clr u_X22 (.CLR(CLR), .D(WD), .CLK(CLK), .EN(decoder_1_out_22), .Q(X22));
  _64_bit_reg_clr u_X23 (.CLR(CLR), .D(WD), .CLK(CLK), .EN(decoder_1_out_23), .Q(X23));
  _64_bit_reg_clr u_X24 (.CLR(CLR), .D(WD), .CLK(CLK), .EN(decoder_1_out_24), .Q(X24));
  _64_bit_reg_clr u_X25 (.CLR(CLR), .D(WD), .CLK(CLK), .EN(decoder_1_out_25), .Q(X25));
  _64_bit_reg_clr u_X26 (.CLR(CLR), .D(WD), .CLK(CLK), .EN(decoder_1_out_26), .Q(X26));
  _64_bit_reg_clr u_X27 (.CLR(CLR), .D(WD), .CLK(CLK), .EN(decoder_1_out_27), .Q(X27));
  _64_bit_reg_clr u_X28 (.CLR(CLR), .D(WD), .CLK(CLK), .EN(decoder_1_out_28), .Q(X28));
  _64_bit_reg_clr u_X29 (.CLR(CLR), .D(WD), .CLK(CLK), .EN(decoder_1_out_29), .Q(X29));
  _64_bit_reg_clr u_X30 (.CLR(CLR), .D(WD), .CLK(CLK), .EN(decoder_1_out_30), .Q(X30));
  _64_bit_reg_clr u_X31 (.CLR(CLR), .D(WD), .CLK(CLK), .EN(decoder_1_out_31), .Q(X31));
  Multiplexer #(.Selector_Bits(5), .Bits(64)) multiplexer_2 (
    .sel(RR0), .in_0({64{1'b0}}), .in_1(X1), .in_2(X2), .in_3(X3), .in_4(X4), .in_5(X5), .in_6(X6),
    .in_7(X7), .in_8(X8), .in_9(X9), .in_10(X10), .in_11(X11), .in_12(X12), .in_13(X13), .in_14(X14),
    .in_15(X15), .in_16(X16), .in_17(X17), .in_18(X18), .in_19(X19), .in_20(X20), .in_21(X21), .in_22(X22),
    .in_23(X23), .in_24(X24), .in_25(X25), .in_26(X26), .in_27(X27), .in_28(X28), .in_29(X29), .in_30(X30),
    .in_31(X31), .out(RD0));
  Multiplexer #(.Selector_Bits(5), .Bits(64)) multiplexer_3 (
    .sel(RR1), .in_0({64{1'b0}}), .in_1(X1), .in_2(X2), .in_3(X3), .in_4(X4), .in_5(X5), .in_6(X6),
    .in_7(X7), .in_8(X8), .in_9(X9), .in_10(X10), .in_11(X11), .in_12(X12), .in_13(X13), .in_14(X14),
    .in_15(X15), .in_16(X16), .in_17(X17), .in_18(X18), .in_19(X19), .in_20(X20), .in_21(X21), .in_22(X22),
    .in_23(X23), .in_24(X24), .in_25(X25), .in_26(X26), .in_27(X27), .in_28(X28), .in_29(X29), .in_30(X30),
    .in_31(X31), .out(RD1));

  assign X0 = {64{1'b0}};
endmodule
