// Digital circuit rv64_cpu.dig as structural Verilog
module rv64_cpu (
  input  EN,
  input  CLK,
  input  CLR,
  input  [4:0] PROG,
  output [63:0] A0,
  output [63:0] A1,
  output [63:0] A2,
  output DONE
);

  wire and_1_out, and_2_out, bcu_1_p4, inst_decoder_1_alusrca, inst_decoder_1_ld, inst_decoder_1_m2r,
       inst_decoder_1_rfw, inst_decoder_1_st, inst_decoder_1_wdsel;
  wire [1:0] inst_decoder_1_pcsel, inst_decoder_1_sz;
  wire [2:0] inst_decoder_1_alusrcb, inst_decoder_1_brop;
  wire [3:0] inst_decoder_1_aluop;
  wire [4:0] reg_decoder_1_rd, reg_decoder_1_rs1, reg_decoder_1_rs2;
  wire [7:0] PC_q_2;
  wire [31:0] IW;
  wire [63:0] add_1_s, alu_1_r, imm_decoder_1_imm_b, imm_decoder_1_imm_i, imm_decoder_1_imm_j,
       imm_decoder_1_imm_s, imm_decoder_1_imm_u, imm_decoder_1_shamt, load_1_dcur, load_1_dout,
       multiplexer_1_out, multiplexer_2_out, multiplexer_3_out, multiplexer_4_out, multiplexer_5_out,
       multiplexer_6_out, PC_q, ramdualport_1_d, reg_file_1_rd0, reg_file_1_rd1, store_1_dout, X0, X1, X2,
       X3, X4, X5, X6, X7, X8, X9, X13, X14, X15, X16, X17, X18, X19, X20, X21, X22, X23, X24, X25, X26, X27,
       X28, X29, X30, X31;

  Multiplexer #(.Bits(64)) multiplexer_1 (
    .sel(bcu_1_p4), .in_0(add_1_s), .in_1({multiplexer_6_out[63:1], 1'b0}), .out(multiplexer_1_out));
  // Probe on X0
  // Probe on X1
  // Probe on X2
  // Probe on X3
  // Probe on X4
  // Probe on X5
  // Probe on X6
  // Probe on X7
  Multiplexer #(.Selector_Bits(2), .Bits(64)) multiplexer_2 (
    .sel(inst_decoder_1_pcsel), .in_0(add_1_s), .in_1(multiplexer_1_out), .in_2({64{1'b0}}),
    .in_3({64{1'b0}}), .out(multiplexer_2_out));
  _64_bit_reg_clr PC (
    .CLR(CLR), .D(multiplexer_2_out), .CLK(and_1_out), .EN(1'b1), .Q({PC_q[63:10], PC_q_2, PC_q[1:0]}));
  // Probe on X8
  // Probe on X9
  // Probe on A0
  // Probe on A1
  // Probe on A2
  // Probe on X13
  // Probe on X14
  // Probe on X15
  Add #(.Bits(64)) add_1 (.a({PC_q[63:10], PC_q_2, PC_q[1:0]}), .b(64'h4), .c_i(1'b0), .s(add_1_s));  // open: c_o
  // Probe on X16
  // Probe on X17
  // Probe on X18
  // Probe on X19
  // Probe on X20
  // Probe on X21
  // Probe on X22
  // Probe on X23
  inst_mem inst_mem_1 (.PROG(PROG), .ADDR(PC_q_2), .IW(IW));
  // Probe on X24
  // Probe on X25
  // Probe on X26
  // Probe on X27
  // Probe on X28
  // Probe on X29
  // Probe on X30
  // Probe on X31
  Comparator #(.Bits(32)) comparator_1 (.a(32'hc0001073), .b(IW), .eq(DONE));  // open: gt, lt
  // Probe on IW
  and and_1 (and_1_out, CLK, ~DONE);  // And
  inst_decoder inst_decoder_1 (
    .IW(IW), .PCsel(inst_decoder_1_pcsel), .SZ(inst_decoder_1_sz), .ST(inst_decoder_1_st),
    .LD(inst_decoder_1_ld), .m2r(inst_decoder_1_m2r), .ALUOp(inst_decoder_1_aluop),
    .ALUSrcA(inst_decoder_1_alusrca), .ALUSrcB(inst_decoder_1_alusrcb), .BrOp(inst_decoder_1_brop),
    .RFW(inst_decoder_1_rfw), .WDsel(inst_decoder_1_wdsel));
  reg_decoder reg_decoder_1 (.IW(IW), .RS1(reg_decoder_1_rs1), .RS2(reg_decoder_1_rs2), .RD(reg_decoder_1_rd));
  imm_decoder imm_decoder_1 (
    .IW(IW), .imm_i(imm_decoder_1_imm_i), .imm_s(imm_decoder_1_imm_s), .imm_b(imm_decoder_1_imm_b),
    .imm_u(imm_decoder_1_imm_u), .imm_j(imm_decoder_1_imm_j), .shamt(imm_decoder_1_shamt));
  Multiplexer #(.Bits(64)) multiplexer_3 (
    .sel(inst_decoder_1_wdsel), .in_0(add_1_s), .in_1(multiplexer_6_out), .out(multiplexer_3_out));
  and and_2 (and_2_out, inst_decoder_1_rfw, EN);
  reg_file reg_file_1 (
    .RR0(reg_decoder_1_rs1), .RR1(reg_decoder_1_rs2), .WREG(reg_decoder_1_rd), .WEN(and_2_out),
    .WD(multiplexer_3_out), .CLK(and_1_out), .CLR(CLR), .RD0(reg_file_1_rd0), .RD1(reg_file_1_rd1), .X0(X0),
    .X1(X1), .X2(X2), .X3(X3), .X4(X4), .X5(X5), .X6(X6), .X7(X7), .X8(X8), .X9(X9), .X10(A0), .X11(A1),
    .X12(A2), .X13(X13), .X14(X14), .X15(X15), .X16(X16), .X17(X17), .X18(X18), .X19(X19), .X20(X20),
    .X21(X21), .X22(X22), .X23(X23), .X24(X24), .X25(X25), .X26(X26), .X27(X27), .X28(X28), .X29(X29),
    .X30(X30), .X31(X31));
  // bcu bcu_1: pin names not known; wires that end beside it: reg_file_1_rd1, reg_file_1_rd0, inst_decoder_1_brop, bcu_1_p4
  Multiplexer #(.Selector_Bits(3), .Bits(64)) multiplexer_4 (
    .sel(inst_decoder_1_alusrcb), .in_0(reg_file_1_rd1), .in_1(imm_decoder_1_imm_i),
    .in_2(imm_decoder_1_imm_s), .in_3(imm_decoder_1_imm_b), .in_4(imm_decoder_1_imm_u),
    .in_5(imm_decoder_1_imm_j), .in_6(imm_decoder_1_shamt), .in_7({64{1'b0}}), .out(multiplexer_4_out));
  Multiplexer #(.Bits(64)) multiplexer_5 (
    .sel(inst_decoder_1_alusrca), .in_0(reg_file_1_rd0), .in_1({PC_q[63:10], PC_q_2, PC_q[1:0]}),
    .out(multiplexer_5_out));
  alu alu_1 (.OP(inst_decoder_1_aluop), .A(multiplexer_5_out), .B(multiplexer_4_out), .R(alu_1_r));
  // Probe on multiplexer_4_out
  Multiplexer #(.Bits(64)) multiplexer_6 (
    .sel(inst_decoder_1_m2r), .in_0(alu_1_r), .in_1(load_1_dout), .out(multiplexer_6_out));
  store store_1 (.A(alu_1_r), .DCur(load_1_dcur), .D(reg_file_1_rd1), .SZ(inst_decoder_1_sz), .DOut(store_1_dout));
  RAMDualPort #(.AddrBits(7), .Bits(64)) ramdualport_1 (
    .A(alu_1_r[9:3]), .Din(store_1_dout), .str(inst_decoder_1_st), .C(and_1_out), .ld(inst_decoder_1_ld),
    .D(ramdualport_1_d));
  load load_1 (.A(alu_1_r), .D(ramdualport_1_d), .DOut(load_1_dout), .DCur(load_1_dcur), .SZ(inst_decoder_1_sz));

  // Other names for the same wires on the sheet: X10[63:0] = A0; X11[63:0] = A1; X12[63:0] = A2
endmodule
