// Digital circuit store.dig as structural Verilog
module store (
  input  [63:0] D,
  input  [63:0] DCur,
  input  [63:0] A,
  input  [1:0] SZ,
  output [63:0] DOut
);

  wire [63:0] multiplexer_1_out, multiplexer_2_out;

  Multiplexer #(.Selector_Bits(3), .Bits(64)) multiplexer_1 (
    .sel(A[2:0]), .in_0({DCur[63:8], D[7:0]}), .in_1({DCur[63:16], D[7:0], DCur[7:0]}),
    .in_2({DCur[63:24], D[7:0], DCur[15:0]}), .in_3({DCur[63:32], D[7:0], DCur[23:0]}),
    .in_4({DCur[63:40], D[7:0], DCur[31:0]}), .in_5({DCur[63:48], D[7:0], DCur[39:0]}),
    .in_6({DCur[63:56], D[7:0], DCur[47:0]}), .in_7({D[7:0], DCur[55:0]}), .out(multiplexer_1_out));
  Multiplexer #(.Bits(64)) multiplexer_2 (
    .sel(A[2]), .in_0({DCur[63:32], D[31:0]}), .in_1({D[31:0], DCur[31:0]}), .out(multiplexer_2_out));
  Multiplexer #(.Selector_Bits(2), .Bits(64)) multiplexer_3 (
    .sel(SZ), .in_0(multiplexer_1_out), .in_1({64{1'b0}}), .in_2(multiplexer_2_out), .in_3(D), .out(DOut));
endmodule
